# Fritzing sketch greenhouse (saved by Fritzing 0.9.10b)
breadboards: 1

parts:
  DHT2 = DHT11 Humitidy and Temperature Sensor
  KY-1 = Keyes Relay [package=THT]
  KY-2 = Keyes Relay [package=THT]
  KY-3 = Keyes Relay [package=THT]
  Εξάρτημα2 = FC-28 Soil Hygrometer Module - Probe
  Εξάρτημα3 = FC-28 Soil Hygrometer Module
  M1 = DC Motor [voltage_(max)=6V voltage_(min)=3V]
  M3 = DC Motor [voltage_(max)=6V voltage_(min)=3V]
  J1 = Basic Servo
  LED1 = smd LED [color="Red (633nm)" package="0603 [SMD]"]
  R1 = Resistor [tolerance=±5% resistance=220 package="2512 [SMD]"]
  Mod1 = Amica NodeMCU DEVKIT 1.0
  Mod2 = KY-018 Photoresistor Module [package="Breakout board"]

nets:
  VCC: DHT2.VDD, KY-1.power, KY-2.power, KY-3.power, Εξάρτημα3.VCC, J1.vcc, Mod1.pin1, Mod1.pin_10, Mod1.pin_26, Mod2.Vin
  N1: DHT2.DATA, Mod1.pin_11
  GND: DHT2.GND, KY-1.ground, KY-2.ground, KY-3.ground, Εξάρτημα3.GND, M1.pin_2, M3.pin_2, J1.gnd, LED1.cathode, Mod1.pin2, Mod1.pin_9, Mod1.pin_25, Mod1.pin_29, Mod2.-
  N2: KY-1.signal, Mod1.pin7
  N3: KY-1.C, M1.pin_1
  N4: KY-1.NO, KY-2.NO, KY-3.NO, Mod1.pin_30
  N5: KY-2.signal, Mod1.pin6
  N6: KY-2.C, M3.pin_1
  N7: KY-3.signal, Mod1.pin8
  N8: KY-3.C, R1.Pin_1
  N9: Εξάρτημα2.POS, Εξάρτημα3.POS
  N10: Εξάρτημα2.NEG, Εξάρτημα3.NEG
  N11: Εξάρτημα3.DO, Mod1.pin_15
  N12: Εξάρτημα3.AO, Mod1.pin_16
  N13: J1.pulse, Mod1.pin_13
  N14: LED1.anode, R1.Pin_0
  N15: Mod1.pin_14, Mod2.S

notes:
  5 volt DC Supply
  DHT11
  LDR
  Soil Moisture Detector Sensor
  ESP8266
  Servo Motor
  Fan
  Water Pump

custom parts:
  DHT11 Humitidy and Temperature Sensor: DHT11 Humidity and Temperature Sensor
  Keyes Relay: The Keyes 5V relay module is suitable for SCM development, home appliance control. It uses a 5V~12V TIL control signal which can control DC / AC signal.
  FC-28 Soil Hygrometer Module - Probe: The FC-28 is a soil hygrometer module that uses the Texas Instruments LM393 comparator chip to provide an analog measurement of soil humidity.
  FC-28 Soil Hygrometer Module: The FC-28 is a soil hygrometer module that uses the Texas Instruments LM393 comparator chip to provide an analog measurement of soil humidity. The digital output is high when soil moisture is over a certain threshold, as determined by adjusting the potentiometer.
  KY-018 Photoresistor Module: KY-018 Photoresistor module, used to measure light intensity. It can determine the presence or absence of light.

// code stored in the sketch: GreenHouse1.8_par1.ino
/*
  ############################################################
  #   File:       GreenHouse1.8_par1.ino                     #
  #   Processor:  Arduino UNO, MEGA                          #
  #   Language:   Wiring / C / Arduino IDE                   #
  #   Objectives: Heating - Aeration - Irrigation            #
  #   Behavior:   Event when the temperature is low          #
  #               or high and the soil is dry                #
  #   Note:       1.8 TFT LCD 128?160                        #
  #               DHT-11 Sensor of Temperature and Humitide  #
  #               DHT-21 Sensor of Temperature and Humitide  #
  #               Soil Moisture Sensor and Hygrometer Module #
  #               Potentiometer1 change limit Moisture       #
  #               Potentiometer2 change limit Temperature    #
  #               Relay1_AirIn to Blower Fan IN              #
  #               Relay2_AirOut to Blower Fan OUT            #
  #               Relay3_Lamp to Hot Lamp                    #
  #               Relay4_Water to Water Pump                 #
  #                                                          #
  #   Author:     Billy Gkekas                               #
  #   Date:       Saturday, 29-10-2018                       #
  #   place:      Greece, Ptolemaida                         #
  #                                                          #
  #   This project contains public domain code.              #
  #   The modification is allowed without notice.            #
  ############################################################
*/
// DHT11 and DHT21 Simoultanouesly (?????????)
#include <DHT.h>
#define DHT11PIN 1
#define DHT21PIN 3
// #define DHT22PIN 2

#define DHT11TYPE DHT11     // DHT 11)
#define DHT21TYPE DHT21   // DHT 21 (AM2301)
// #define DHT22TYPE DHT22   // DHT 22 (AM2302), AM2321

DHT dht11(DHT11PIN, DHT11TYPE); // Initialize DHT11 sensor for normal 16mhz Arduino
DHT dht21(DHT21PIN, DHT21TYPE); // Initialize DHT22 sensor for normal 16mhz Arduino
// ************************************************************************

// 1.8 TFT LCD 128X 160
#include  <Adafruit_GFX.h>
#include  <Adafruit_ST7735.h>
#include <SPI.h>

#define BLACK   0x0000
#define BLUE    0x001F
#define RED     0xF800
#define GREEN   0x07E0
#define MAGENTA 0xF81F
#define YELLOW  0xFFE0
#define WHITE   0xFFFF
#define GRAY    0x7BEF
#define LIGHT_GRAY 0xC618
#define LIME    0x87E0
#define AQUA    0x5D1C
#define CYAN    0x07FF
#define DARK_CYAN 0x03EF
#define ORANGE  0xFCA0
#define PINK    0xF97F
#define BROWN   0x8200
#define VIOLET  0x9199
#define SILVER  0xA510
#define GOLD    0xA508
#define NAVY    0x000F
#define MAROON  0x7800
#define PURPLE  0x780F
#define OLIVE   0x7BE0

#define TFT_SCLK  13
#define TFT_MOSI  11
#define TFT_CS    10
#define TFT_RST    9
#define TFT_DC     8

Adafruit_ST7735 tft = Adafruit_ST7735(TFT_CS,  TFT_DC, TFT_RST);

// Variable Definitions
float temp_external = 22;
float hum_external = 55;
float temp_internal;
float hum_internal;

int readSoil() ;
int PinState;           // Condition of pins (??????? ??? ???? ?? ?? ????????? ????? HIGH ? LOW)
int valMoisture = 0;    // Stores Soil Moisture value (???? ???????? ???)
int kath = 5000;        // Delay (???????????)
int LimM = 1023 ;       // Stores value after edit (????????? ???? ????????)
int LimT = 25 ;         // Stores value after edit (????????? ???? ????????????)
int manytimes = 1;      // ????????? ??? ???? 1 ?? ???? ?????????
int total;              // ????????? ???????????

//pin definitions
int MoisturePin = A0;   // Moisture Analog pin
int potention1 = A1;    // Potentiometer to change Temperature Limit
int potention2 = A2;    // Potentiometer to change Moisture Limit
int Relay1_AirIn = 4;   // airRelay1 Blower Air Fan IN
int Relay2_AirOut = 5;  // airRelay2 Blower Air Fan OUT
int Relay3_Lamp = 6;    // Relay3_Lamp Hot Lamp
int Relay4_Water = 7;   // Relay4_Water Pump
int soilPower = 2;      // Moisture Soil power
// *******************************************************

void setup() {
  Serial.begin(9600);

  dht11.begin();  // DHT11 Starts
  dht21.begin();  // DHT21 Starts
  // dht22.begin();  // DHT22 Starts

  tft.initR(INITR_BLACKTAB);  // Initialize 1.8 TFT LCD 128 X 160
  tft.fillScreen(BLACK);
  tft.setRotation(0);

  // Initialize Sensor Moisture
  pinMode(soilPower, OUTPUT);   // Set D2 as an OUTPUT
  digitalWrite(soilPower, LOW); // Set to LOW, no power in the sensor

  // Initialize Pins
  pinMode(potention1, INPUT);
  pinMode(potention2, INPUT);
  pinMode(Relay1_AirIn, OUTPUT);
  pinMode(Relay2_AirOut, OUTPUT);
  pinMode(Relay3_Lamp, OUTPUT);
  pinMode(Relay4_Water, OUTPUT);

  digitalWrite(Relay1_AirIn, LOW);
  digitalWrite(Relay2_AirOut, LOW);
  digitalWrite(Relay3_Lamp, LOW);
  digitalWrite(Relay4_Water, LOW);
}

void loop() {
  Sensors();        // Read values from sensors
  Show_Values();    // Send on Screen and Serial values

  Serial.print("Soil: ");
  Serial.println(valMoisture);
  printText("SOIL", WHITE, 2, 83, 2);
  printText("WATER", WHITE, 5, 143, 2);

  CheckSoil();

  printText("AIR ", WHITE, 2, 103, 2);
  printText("LAMP", WHITE, 5, 123, 2);
  CheckConditions();

  manytimes++;
  total++;

  if (manytimes == 50) {
    Refresh_Screen();
  }
  delay(kath);
  tft.setTextSize(1);
  tft.fillRect(50, 80, 128, 40, BLACK);
  tft.setTextColor(WHITE);
}

void Show_Values() {
  // Print readed values of External and Internal Temperature
  tft.fillRect(0, 0, 64, 20, RED);
  printText1(temp_external, WHITE, 2, 2, 2);
  tft.fillRect(64, 0, 64, 20, MAGENTA);
  printText1(temp_internal, WHITE, 66, 2, 2);
  tft.fillRect(43, 20, 45, 20, CYAN);
  printText("EXT", WHITE, 2, 23, 2);
  tft.setCursor(50, 23);
  tft.setTextColor(BLACK);
  tft.print(LimT);
  printText("INT", WHITE, 90, 23, 2);

  // ***************************************************************************

  // Print readed values of Internal and Internal Humidity
  tft.fillRect(0, 40, 64, 20, VIOLET);
  printText1(hum_external, WHITE, 2, 43, 2);
  tft.fillRect(64, 40, 64, 20, YELLOW);
  printText1(hum_internal, BLACK, 66, 43, 2);
  tft.fillRect(58, 60, 128, 20, CYAN);
  printText("LimM", WHITE, 2, 63, 2);
  tft.setCursor(65, 63);
  tft.setTextColor(BLACK);
  tft.print(LimM);
  tft.print(" %");

  // Print on Serial Window readed values
  Serial.print("Counter = ");
  Serial.println(manytimes);
  Serial.print("TOTAL = ");
  Serial.println(total);
  PinState = digitalRead(Relay1_AirIn);
  Serial.print("Air In = ");
  Serial.println(PinState);
  PinState = digitalRead(Relay2_AirOut);
  Serial.print("Air Out = ");
  Serial.println(PinState);
  PinState = digitalRead(Relay3_Lamp);
  Serial.print("Lamp = ");
  Serial.println(PinState);
  PinState = digitalRead(Relay4_Water);
  Serial.print("Water = ");
  Serial.println(PinState);
  Serial.println("");
}

void Sensors() {
  // Read data from DHT Sensors
  //  temp_external = dht11.readTemperature();
  //  hum_external = dht11.readHumidity();
  temp_internal = dht21.readTemperature();
  hum_internal = dht21.readHumidity();

  // This Function send power and then reads from Soil Moisture Sensor
  // int readSoil() ;
  digitalWrite(soilPower, HIGH); // turn D2 "On"
  delay(10); // wait 10 milliseconds giving time to Moisture Sensor
  // Read the SIGNAL value (data) from the sensor and counted percent degrees
  valMoisture = analogRead(MoisturePin) * 0.1;
  digitalWrite(soilPower, LOW); // turn power on D2 "Off"

  // Read from potentiometers limit of Temperature and Humidity
  LimT = analogRead(potention1) * 0.1;  // Read limit from Potentiometer
  LimM = analogRead(potention2) * 0.1; // Read limit from Potentiometer

}

void Refresh_Screen() {
  tft.fillScreen(BLACK);
  printText("Smart", LIME, 15, 20, 2);
  printText("GreenHouse", GREEN, 5, 50, 2);
  printText("v4.0", AQUA, 15, 80, 2);
  delay(3000);
  manytimes = 0;
}

void CheckSoil() {
  if (valMoisture >= LimM) {
    digitalWrite(Relay4_Water, HIGH);
    tft.fillRect(58, 80, 128, 20, BLUE);
    printText1(valMoisture, WHITE, 65, 83, 2);
    tft.fillRect(80, 140, 128, 20, GREEN);
    printText("ON", BLACK, 85, 143, 2);
  }
  else {
    digitalWrite(Relay4_Water, LOW);
    tft.fillRect(58, 80, 128, 20, BLUE);
    printText1(valMoisture, WHITE, 65, 83, 2);
    tft.fillRect(80, 140, 128, 20, RED);
    printText("OFF", WHITE, 85, 143, 2);
  }
}

void CheckConditions() {
  if (temp_internal >= LimT) {
    if (temp_internal > temp_external) {
      Serial.println("1. t_int >= LimT & t_int > t_ext");
      Serial.print(temp_internal);
      Serial.print(" >= ");
      Serial.print(LimT);
      Serial.print(" & > ");
      Serial.print(temp_external);
      Serial.println("   AirIn On - AirOut On - Lamp Off");

      tft.fillRect(40, 100, 42, 20, GREEN);
      printText("IN ", BLACK, 45, 103, 2);
      PinState = digitalRead(Relay1_AirIn);
      if (PinState == 1) {
        // do nothing
      }
      else {
        digitalWrite(Relay1_AirIn, HIGH);
      }

      tft.fillRect(80, 100, 128, 20, GREEN);
      printText("OUT", BLACK, 85, 103, 2);
      PinState = digitalRead(Relay2_AirOut);
      if (PinState == 1) {
        // do nothing

      }
      else {
        digitalWrite(Relay2_AirOut, HIGH);
      }

      tft.fillRect(80, 120, 128, 20, RED);
      printText("OFF", WHITE, 85, 123, 2);
      PinState = digitalRead(Relay3_Lamp);
      if (PinState == 0) {
        // do nothing
      }
      else {
        digitalWrite(Relay3_Lamp, LOW);
      }
    }
    else {
      Serial.println("else 1. t_int >= LimT & t_int < t_ext");
      Serial.print(temp_external);
      Serial.print(" > ");
      Serial.print(temp_internal);
      Serial.print(" >= ");
      Serial.print(LimT);
      Serial.println("   AirIn Off - AirOut On - Lamp Off");

      tft.fillRect(40, 100, 42, 20, RED);
      printText("IN ", WHITE, 45, 103, 2);
      PinState = digitalRead(Relay1_AirIn);
      if (PinState == 0) {
        // do nothing
      }
      else {
        digitalWrite(Relay1_AirIn, LOW);
      }
      tft.fillRect(80, 100, 128, 20, GREEN);
      printText("OUT", BLACK, 85, 103, 2);
      PinState = digitalRead(Relay2_AirOut);
      if (PinState == 1) {
        // do nothing
      }
      else {
        digitalWrite(Relay2_AirOut, HIGH);
      }

      tft.fillRect(80, 120, 128, 20, RED);
      printText("OFF", WHITE, 85, 123, 2);
      PinState = digitalRead(Relay3_Lamp);
      if (PinState == 0) {
        // do nothing
      }
      else {
        digitalWrite(Relay3_Lamp, LOW);
      }
    }
  }

  if (temp_internal < LimT) {
    if (temp_internal <= temp_external) {
      Serial.println("2. t_int < LimT & t_int >= t_ext");
      Serial.print(temp_external);
      Serial.print(" <= ");
      Serial.print(temp_internal);
      Serial.print(" < ");
      Serial.print(LimT);
      Serial.println("   AirIn ON - AirOut Off - Lamp On");

      tft.fillRect(40, 100, 42, 20, GREEN);
      printText("IN", BLACK, 50, 103, 2);
      if (PinState == 1) {
        // do nothing
      }
      else {
        digitalWrite(Relay1_AirIn, HIGH);
      }

      tft.fillRect(80, 100, 128, 20, RED);
      printText("OUT", WHITE, 85, 103, 2);
      PinState = digitalRead(Relay2_AirOut);
      if (PinState == 0) {
        // do nothing
      }
      else {
        digitalWrite(Relay2_AirOut, LOW);
      }

      tft.fillRect(80, 120, 128, 20, GREEN);
      printText("ON", BLACK, 85, 123, 2);
      PinState = digitalRead(Relay3_Lamp);
      if (PinState == 1) {
        // do nothing
      }
      else {
        digitalWrite(Relay3_Lamp, HIGH);
      }
    }
    else {
      Serial.println("else 2. t_int < LimT & t_int < t_ext");
      Serial.print(temp_internal);
      Serial.print(" < ");
      Serial.print(LimT);
      Serial.print(" & ");
      Serial.print(temp_external);
      Serial.println("AirIn OFF - AirOut Off - Lamp On");

      tft.fillRect(40, 100, 42, 20, RED);
      printText("IN", WHITE, 44, 103, 2);
      PinState = digitalRead(Relay1_AirIn);
      if (PinState == 0) {
        // do nothing
      }
      else {
        digitalWrite(Relay1_AirIn, LOW);
      }

      tft.fillRect(80, 100, 128, 20, RED);
      printText("OUT", WHITE, 85, 103, 2);
      PinState = digitalRead(Relay2_AirOut);
      if (PinState == 0) {
        // do nothing
      }
      else {
        digitalWrite(Relay2_AirOut, LOW);
      }

      tft.fillRect(80, 120, 128, 20, RED);
      printText("OFF", WHITE, 85, 123, 2);
      PinState = digitalRead(Relay3_Lamp);
      if (PinState == 1) {
        // do nothing
      }
      else {
        digitalWrite(Relay3_Lamp, HIGH);
      }
    }
  }
}

// ***************************************************************************
// Function Print Text
void printText(char *text, uint16_t color, int x, int y, int textSize)
{
  tft.setCursor(x, y);
  tft.setTextColor(color);
  tft.setTextSize(textSize);
  tft.setTextWrap(true);
  tft.print(text);
  // printText("MAX", RED,18,130,1);
}

// ***************************************************************************
// Function Print float
void printText1(float num, uint16_t color, int x, int y, int textSize)
{
  tft.setCursor(x, y);
  tft.setTextColor(color);
  tft.setTextSize(textSize);
  tft.setTextWrap(true);
  tft.print(num);
  // printText1(value, RED,18,130,1);
}
